// Digital circuit decoder.dig as structural Verilog
module decoder (
  input  [31:0] Instruction,
  output [15:0] A,
  output [3:0] rs,
  output [3:0] rd
);

  // Pins of 2 and 4 bits meet at {rs[3:2], Instruction[21:20]}
  // Pins of 2 and 4 bits meet at {rd[3:2], Instruction[17:16]}

  assign A = Instruction[15:0];
  assign rd[1:0] = Instruction[17:16];
  assign rs[1:0] = Instruction[21:20];
endmodule
