// Digital circuit executor.dig as structural Verilog
module executor (
  input  [15:0] A,
  input  [15:0] B,
  output [15:0] result
);

  Add #(.Bits(16)) add_1 (.a(A), .b(B), .c_i(1'b0), .s(result));  // open: c_o
endmodule
